# Fritzing sketch SmartParking_Schematic (saved by Fritzing 0.9.3b)
breadboards: 1

parts:
  J1 = Basic Servo
  Part1 = RFID-RC522-v3
  LED1 = LED - 3mm [color="Green (555nm)" package="3 mm [THT]"]
  LED2 = LED - 3mm [color="Red (633nm)" package="3 mm [THT]"]
  LED3 = LED - 3mm [color="Blue (470nm)" package="3 mm [THT]"]
  U1 = NodeMCU V1.0

nets:
  GND: J1.gnd, Part1.GND, LED1.cathode, LED2.cathode, LED3.cathode, U1.GND
  VCC: J1.vcc, Part1.3.3V, U1.3V3
  N1: J1.pulse, U1.D2
  N2: Part1.SDA, U1.D8
  N3: Part1.SCK, U1.D5
  N4: Part1.MOSI, U1.D7
  N5: Part1.MISO, U1.D6
  N6: Part1.RST, U1.D3
  N7: LED1.anode, U1.D0
  N8: LED2.anode, U1.D1
  N9: LED3.anode, U1.D4

notes:
  Smart Part System made by Mayank Narang.

custom parts:
  RFID-RC522-v3: A simple China made RFID-RC522 Reader (6x4 cm); do check the pin labels, as this is a MFRC522 based clone.
  NodeMCU V1.0: ESP8266 based NodeMCU
